// Digital circuit 5Bit-Adder.dig as structural Verilog
module _5Bit_Adder (
  input  A0,
  input  A1,
  input  A2,
  input  A3,
  input  B0,
  input  B1,
  input  B2,
  input  B3,
  output S0,
  output S1,
  output S2,
  output S3,
  output Cout
);

  wire full_adder_1_cout, full_adder_2_cout, full_adder_3_cout;

  Full_Adder full_adder_1 (.A(A0), .B(B0), .Cin(1'b0), .S(S0), .Cout(full_adder_1_cout));
  Full_Adder full_adder_2 (.A(A1), .B(B1), .Cin(full_adder_1_cout), .S(S1), .Cout(full_adder_2_cout));
  Full_Adder full_adder_3 (.A(A2), .B(B2), .Cin(full_adder_2_cout), .S(S2), .Cout(full_adder_3_cout));
  Full_Adder full_adder_4 (.A(A3), .B(B3), .Cin(full_adder_3_cout), .S(S3), .Cout(Cout));
endmodule
