// Digital circuit 5Bit-ComparatorSM.dig as structural Verilog
module _5Bit_ComparatorSM (
  input  A0,
  input  A1,
  input  A2,
  input  A3,
  input  A4,
  input  B0,
  input  B1,
  input  B2,
  input  B3,
  input  B4,
  output Y
);

  wire and_1_out, and_2_out, nor_1_out, nor_2_out, xnor_1_out, xnor_2_out, xnor_3_out, xnor_4_out, xnor_5_out;

  xnor xnor_1 (xnor_1_out, A4, B4);
  xnor xnor_2 (xnor_2_out, A3, B3);
  xnor xnor_3 (xnor_3_out, A2, B2);
  xnor xnor_4 (xnor_4_out, A1, B1);
  xnor xnor_5 (xnor_5_out, A0, B0);
  nor nor_1 (nor_1_out, A3, A2, A1, A0);
  nor nor_2 (nor_2_out, B3, B2, B1, B0);
  and and_1 (and_1_out, xnor_1_out, xnor_2_out, xnor_3_out, xnor_4_out, xnor_5_out);
  and and_2 (and_2_out, nor_1_out, nor_2_out);
  or or_1 (Y, and_1_out, and_2_out);
endmodule

/* Test case:
A0 B0 A1 B1 A2 B2 A3 B3 A4 B4 Y
0 0 0 0 0 0 0 0 0 0 1
1 1 0 0 0 0 0 0 0 0 1
1 0 0 0 0 0 0 0 0 0 0
0 0 0 0 0 0 0 0 1 1 1
1 1 0 0 0 0 0 0 1 1 1
1 0 0 0 0 0 0 0 1 1 0
*/
