// Digital circuit Half-Substracter.dig as structural Verilog
module Half_Substracter (
  input  A,
  input  B,
  output S,
  output R
);

  wire not_1_out;

  not not_1 (not_1_out, A);
  xor xor_1 (S, A, B);
  and and_1 (R, not_1_out, B);
endmodule
