// Digital circuit showDisplay.dig as structural Verilog
module showDisplay (
  input  X,
  input  Y,
  output A,
  output B,
  output C,
  output D,
  output E,
  output F,
  output G
);

  wire and_1_out, and_2_out, not_1_out, not_2_out;

  not not_1 (not_1_out, X);
  not not_2 (not_2_out, Y);
  and and_1 (and_1_out, not_1_out, not_2_out);
  and and_2 (and_2_out, X, Y);
  or or_1 (C, not_1_out, not_2_out);
  and and_3 (F, not_1_out, not_2_out);
  and and_4 (G, X, Y);
  or or_2 (A, and_1_out, and_2_out);

  assign B = 1'b1;
  assign D = A;
  assign E = A;
endmodule

/* Test case:
X Y A B C D E F G
0 0 1 1 1 1 1 1 0
0 1 0 1 1 0 0 0 0
1 0 0 1 1 0 0 0 0
1 1 1 1 0 1 1 0 1
*/
