// Digital circuit Template.dig as structural Verilog
module Template (
  input  Mode,
  input  Pup,
  input  Pdw,
  input  Cup,
  input  Cdw
);

  // Not not_1 has open pins: in=Mode, out=open
  // Not not_2 has open pins: in=Pup, out=open
  // Not not_3 has open pins: in=Pdw, out=open
  // Not not_4 has open pins: in=Cup, out=open
  // Not not_5 has open pins: in=Cdw, out=open

  // Notes on the sheet:
  //   Mode: 0 ⇢ Manual
  //   1 ⇢ Automatic
endmodule
