// Digital circuit solucio.dig as structural Verilog
module solucio (
  input  Mode,
  input  CLK,
  output CL,
  output PL
);

  wire Cdw_out, codificarentrades_1_x0, codificarentrades_1_x1, codificarentrades_1_x2, Cup_out, Pdw_out,
       pinyodisplay_1_a, pinyodisplay_1_b, pinyodisplay_1_c, pinyodisplay_1_d, pinyodisplay_1_e,
       pinyodisplay_1_f, pinyodisplay_1_g, pinyodisplay_1_h, platedisplay_1_a, platedisplay_1_b,
       platedisplay_1_c, platedisplay_1_d, platedisplay_1_e, platedisplay_1_f, platedisplay_1_g,
       platedisplay_1_h, Pup_out, sequentialcircuit_1_p, sequentialcircuit_1_x, sequentialcircuit_1_y;

  Button Pup (.out(Pup_out));
  Button Pdw (.out(Pdw_out));
  Button Cup (.out(Cup_out));
  Button Cdw (.out(Cdw_out));
  CodificarEntrades codificarentrades_1 (
    .M(Mode), .Pup(Pup_out), .Pdw(Pdw_out), .Cup(Cup_out), .Cdw(Cdw_out), .X2(codificarentrades_1_x2),
    .X1(codificarentrades_1_x1), .X0(codificarentrades_1_x0));
  SequentialCircuit sequentialcircuit_1 (
    .CLK(CLK), .X2(codificarentrades_1_x2), .X1(codificarentrades_1_x1), .X0(codificarentrades_1_x0),
    .P(sequentialcircuit_1_p), .PL(PL), .X(sequentialcircuit_1_x), .Y(sequentialcircuit_1_y), .CL(CL));
  PlateDisplay platedisplay_1 (
    .P(sequentialcircuit_1_p), .A(platedisplay_1_a), .B(platedisplay_1_b), .C(platedisplay_1_c),
    .D(platedisplay_1_d), .E(platedisplay_1_e), .F(platedisplay_1_f), .G(platedisplay_1_g),
    .H(platedisplay_1_h));
  PinyoDisplay pinyodisplay_1 (
    .X(sequentialcircuit_1_x), .Y(sequentialcircuit_1_y), .A(pinyodisplay_1_a), .B(pinyodisplay_1_b),
    .C(pinyodisplay_1_c), .D(pinyodisplay_1_d), .E(pinyodisplay_1_e), .F(pinyodisplay_1_f),
    .G(pinyodisplay_1_g), .H(pinyodisplay_1_h));
  Seven_Seg seven_seg_1 (
    .a(platedisplay_1_a), .b(platedisplay_1_b), .c(platedisplay_1_c), .d(platedisplay_1_d),
    .e(platedisplay_1_e), .f(platedisplay_1_f), .g(platedisplay_1_g), .dp(platedisplay_1_h));
  Seven_Seg seven_seg_2 (
    .a(pinyodisplay_1_a), .b(pinyodisplay_1_b), .c(pinyodisplay_1_c), .d(pinyodisplay_1_d),
    .e(pinyodisplay_1_e), .f(pinyodisplay_1_f), .g(pinyodisplay_1_g), .dp(pinyodisplay_1_h));

  // Notes on the sheet:
  //   Mode: 0 ⇢ Manual
  //   1 ⇢ Automatic
endmodule
