// Digital circuit P1.dig as structural Verilog
module P1 (
  input  A,
  input  B,
  input  C,
  output SOP,
  output POS,
  output NAND
);

  wire and_1_out, and_2_out, nand_1_out, nand_2_out, nand_3_out, nand_4_out, nand_5_out, not_1_out,
       not_2_out, not_3_out, or_1_out, or_2_out;

  not not_1 (not_1_out, A);
  nand nand_1 (nand_1_out, A, A);
  not not_2 (not_2_out, B);
  nand nand_2 (nand_2_out, B, B);
  not not_3 (not_3_out, C);
  nand nand_3 (nand_3_out, C, C);
  and and_1 (and_1_out, not_1_out, not_2_out);
  and and_2 (and_2_out, B, C);
  or or_1 (or_1_out, not_1_out, B);
  or or_2 (or_2_out, not_2_out, C);
  nand nand_4 (nand_4_out, nand_1_out, nand_2_out);
  nand nand_5 (nand_5_out, B, C);
  or or_3 (SOP, and_1_out, and_2_out);
  and and_3 (POS, or_1_out, or_2_out);
  nand nand_6 (NAND, nand_4_out, nand_5_out);

  // Notes on the sheet:
  //   A: A
endmodule

/* Test case:
A B C SOP POS NAND
0 0 0 1 1 1
0 0 1 1 1 1
0 1 0 0 0 0 
0 1 1 1 1 1
1 0 0 0 0 0
1 0 1 0 0 0
1 1 0 0 0 0
1 1 1 1 1 1
*/
