// Digital circuit NAND.dig as structural Verilog
module NAND (
  input  A,
  input  B,
  input  C,
  output Y
);

  wire nand_1_out, nand_2_out, nand_3_out, nand_4_out, nand_5_out;

  nand nand_1 (nand_1_out, A, A);
  nand nand_2 (nand_2_out, B, B);
  nand nand_3 (nand_3_out, C, C);
  nand nand_4 (nand_4_out, nand_1_out, nand_2_out);
  nand nand_5 (nand_5_out, B, C);
  nand nand_6 (Y, nand_4_out, nand_5_out);

  // Notes on the sheet:
  //   A: A
endmodule
