// Digital circuit P1.dig as structural Verilog
module P1 (
  input  A,
  input  B,
  input  C,
  output SOP,
  output POS,
  output NAND
);

  SOP sop_1 (.A(A), .B(B), .C(C), .SOP(SOP));
  POS pos_1 (.A(A), .B(B), .C(C), .Y(POS));
  NAND nand_1 (.A(A), .B(B), .C(C), .Y(NAND));

  // Notes on the sheet:
  //   A: A
endmodule

/* Test case:
A B C SOP POS NAND
0 0 0 1 1 1
0 0 1 1 1 1
0 1 0 0 0 0 
0 1 1 1 1 1
1 0 0 0 0 0
1 0 1 0 0 0
1 1 0 0 0 0
1 1 1 1 1 1
*/
