// Digital circuit POS.dig as structural Verilog
module POS (
  input  A,
  input  B,
  input  C,
  output Y
);

  wire not_1_out, not_2_out, not_3_out, or_1_out, or_2_out;

  not not_1 (not_1_out, A);
  not not_2 (not_2_out, B);
  not not_3 (not_3_out, C);
  or or_1 (or_1_out, not_1_out, B);
  or or_2 (or_2_out, not_2_out, C);
  and and_1 (Y, or_1_out, or_2_out);

  // Notes on the sheet:
  //   A: A
endmodule
