// Digital circuit DECOD.dig as structural Verilog
module DECOD (
  input  X2,
  input  X1,
  input  X0,
  output Y1,
  output Y0
);

  wire decoder_1_out_1, decoder_1_out_2, decoder_1_out_4, decoder_1_out_5, decoder_1_out_7;

  Decoder #(.Selector_Bits(3)) decoder_1 (
    .sel({X2, X1, X0}), .out_1(decoder_1_out_1), .out_2(decoder_1_out_2), .out_4(decoder_1_out_4),
    .out_5(decoder_1_out_5), .out_7(decoder_1_out_7));  // open: out_0, out_3, out_6
  or or_1 (Y1, decoder_1_out_2, decoder_1_out_5);
  or or_2 (Y0, decoder_1_out_1, decoder_1_out_4, decoder_1_out_7);
endmodule

/* Test case:
X2 X1 X0 Y1 Y0
0 0 0 0 0 
0 0 1 0 1
0 1 0 1 0
0 1 1 0 0
1 0 0 0 1
1 0 1 1 0
1 1 0 0 0
1 1 1 0 1
*/
