// Digital circuit NOR.dig as structural Verilog
module NOR (
  input  X2,
  input  X1,
  input  X0,
  output Y1,
  output Y0
);

  wire nor_1_out, nor_2_out, nor_3_out, nor_4_out, nor_5_out, nor_6_out, nor_7_out, nor_8_out, nor_9_out,
       nor_10_out;

  nor nor_1 (nor_1_out, X2, X2);
  nor nor_2 (nor_2_out, X1, X1);
  nor nor_3 (nor_3_out, X0, X0);
  nor nor_4 (nor_4_out, X1, X0);
  nor nor_5 (nor_5_out, X2, nor_3_out);
  nor nor_6 (nor_6_out, nor_1_out, nor_2_out);
  nor nor_7 (nor_7_out, X2, X0);
  nor nor_8 (nor_8_out, X2, nor_2_out);
  nor nor_9 (nor_9_out, nor_2_out, X0);
  nor nor_10 (nor_10_out, nor_1_out, X1, nor_3_out);
  nor nor_11 (Y1, nor_4_out, nor_5_out, nor_6_out);
  nor nor_12 (Y0, nor_7_out, nor_8_out, nor_9_out, nor_10_out);
endmodule

/* Test case:
X2 X1 X0 Y1 Y0
0 0 0 0 0 
0 0 1 0 1
0 1 0 1 0
0 1 1 0 0
1 0 0 0 1
1 0 1 1 0
1 1 0 0 0
1 1 1 0 1
*/
