// Digital circuit P2.dig as structural Verilog
module P2 (
  input  X2,
  input  X1,
  input  X0,
  output Y1,
  output Y0
);

  wire decod_1_y0, decod_1_y1, nor_1_y0, nor_1_y1, sop_1_y0, sop_1_y1;

  SOP sop_1 (.X2(X2), .X1(X1), .X0(X0), .Y1(sop_1_y1), .Y0(sop_1_y0));
  NOR nor_1 (.X2(X2), .X1(X1), .X0(X0), .Y1(nor_1_y1), .Y0(nor_1_y0));
  DECOD decod_1 (.X2(X2), .X1(X1), .X0(X0), .Y1(decod_1_y1), .Y0(decod_1_y0));
  and and_1 (Y1, sop_1_y1, nor_1_y1, decod_1_y1);
  and and_2 (Y0, sop_1_y0, nor_1_y0, decod_1_y0);
endmodule
