// Digital circuit SOP.dig as structural Verilog
module SOP (
  input  X2,
  input  X1,
  input  X0,
  output Y1,
  output Y0
);

  wire and_1_out, and_2_out, and_3_out, and_4_out, and_5_out, not_1_out, not_2_out, not_3_out;

  not not_1 (not_1_out, X2);
  not not_2 (not_2_out, X1);
  not not_3 (not_3_out, X0);
  and and_1 (and_1_out, not_1_out, X1, not_3_out);
  and and_2 (and_2_out, X2, not_2_out, X0);
  and and_3 (and_3_out, not_1_out, not_2_out, X0);
  and and_4 (and_4_out, X2, not_2_out, not_3_out);
  and and_5 (and_5_out, X2, X1, X0);
  or or_1 (Y1, and_1_out, and_2_out);
  or or_2 (Y0, and_3_out, and_4_out, and_5_out);
endmodule

/* Test case:
X2 X1 X0 Y1 Y0
0 0 0 0 0 
0 0 1 0 1
0 1 0 1 0
0 1 1 0 0
1 0 0 0 1
1 0 1 1 0
1 1 0 0 0
1 1 1 0 1
*/
