// Digital circuit 1.dig as structural Verilog
module _1 (
  input  S1,
  input  S0,
  input  S3,
  input  S2,
  input  D0,
  input  D1,
  input  D2,
  input  D3,
  input  D4,
  input  D5,
  input  D6,
  input  D7,
  input  D8,
  input  D9,
  input  D10,
  input  D11,
  input  D12,
  input  D13,
  input  D14,
  input  D15,
  output Y
);

  wire _1_1_y, _1_2_y, _1_3_y, _1_4_y;

  _1 _1_1 (.S1(S1), .S0(S0), .D3(D15), .D2(D14), .D1(D13), .D0(D12), .Y(_1_1_y));
  _1 _1_2 (.S1(S1), .S0(S0), .D3(D11), .D2(D10), .D1(D9), .D0(D8), .Y(_1_2_y));
  _1 _1_3 (.S1(S1), .S0(S0), .D3(D7), .D2(D6), .D1(D5), .D0(D4), .Y(_1_3_y));
  _1 _1_4 (.S1(S1), .S0(S0), .D3(D3), .D2(D2), .D1(D1), .D0(D0), .Y(_1_4_y));
  _1 _1_5 (.S1(S3), .S0(S2), .D3(_1_1_y), .D2(_1_2_y), .D1(_1_3_y), .D0(_1_4_y), .Y(Y));
endmodule

/* Test case:
S3 S2 S1 S0 D0 D1 D2 D3 D4 D5 D6 D7 D8 D9 D10 D11 D12 D13 D14 D15 Y
0 0 0 0 0 1 1 1 1 1 1 1 1 1 1 1 1 1 1 1 0
0 0 0 0 1 0 0 0 0 0 0 0 0 0 0 0 0 0 0 0 1
0 0 0 1 1 0 1 1 1 1 1 1 1 1 1 1 1 1 1 1 0
0 0 0 1 0 1 0 0 0 0 0 0 0 0 0 0 0 0 0 0 1
0 0 1 0 1 1 0 1 1 1 1 1 1 1 1 1 1 1 1 1 0
0 0 1 0 0 0 1 0 0 0 0 0 0 0 0 0 0 0 0 0 1
0 0 1 1 1 1 1 0 1 1 1 1 1 1 1 1 1 1 1 1 0
0 0 1 1 0 0 0 1 0 0 0 0 0 0 0 0 0 0 0 0 1
0 1 0 0 1 1 1 1 0 1 1 1 1 1 1 1 1 1 1 1 0
0 1 0 0 0 0 0 0 1 0 0 0 0 0 0 0 0 0 0 0 1
0 1 0 1 1 1 1 1 1 0 1 1 1 1 1 1 1 1 1 1 0
0 1 0 1 0 0 0 0 0 1 0 0 0 0 0 0 0 0 0 0 1
0 1 1 0 1 1 1 1 1 1 0 1 1 1 1 1 1 1 1 1 0
0 1 1 0 0 0 0 0 0 0 1 0 0 0 0 0 0 0 0 0 1
0 1 1 1 1 1 1 1 1 1 1 0 1 1 1 1 1 1 1 1 0
0 1 1 1 0 0 0 0 0 0 0 1 0 0 0 0 0 0 0 0 1
1 0 0 0 1 1 1 1 1 1 1 1 0 1 1 1 1 1 1 1 0
1 0 0 0 0 0 0 0 0 0 0 0 1 0 0 0 0 0 0 0 1
1 0 0 1 1 1 1 1 1 1 1 1 1 0 1 1 1 1 1 1 0
1 0 0 1 0 0 0 0 0 0 0 0 0 1 0 0 0 0 0 0 1
1 0 1 0 1 1 1 1 1 1 1 1 1 1 0 1 1 1 1 1 0
1 0 1 0 0 0 0 0 0 0 0 0 0 0 1 0 0 0 0 0 1
1 0 1 1 1 1 1 1 1 1 1 1 1 1 1 0 1 1 1 1 0
1 0 1 1 0 0 0 0 0 0 0 0 0 0 0 1 0 0 0 0 1
1 1 0 0 1 1 1 1 1 1 1 1 1 1 1 1 0 1 1 1 0
1 1 0 0 0 0 0 0 0 0 0 0 0 0 0 0 1 0 0 0 1
1 1 0 1 1 1 1 1 1 1 1 1 1 1 1 1 1 0 1 1 0
1 1 0 1 0 0 0 0 0 0 0 0 0 0 0 0 0 1 0 0 1
1 1 1 0 1 1 1 1 1 1 1 1 1 1 1 1 1 1 0 1 0
1 1 1 0 0 0 0 0 0 0 0 0 0 0 0 0 0 0 1 0 1
1 1 1 1 1 1 1 1 1 1 1 1 1 1 1 1 1 1 1 0 0
1 1 1 1 0 0 0 0 0 0 0 0 0 0 0 0 0 0 0 1 1
*/
