// Digital circuit 1.dig as structural Verilog
module _1 (
  input  S1,
  input  S0,
  input  D3,
  input  D2,
  input  D1,
  input  D0,
  output Y
);

  wire and_1_out, and_2_out, and_3_out, and_4_out, not_1_out, not_2_out;

  not not_1 (not_1_out, S1);
  not not_2 (not_2_out, S0);
  and and_1 (and_1_out, D0, not_2_out, not_1_out);
  and and_2 (and_2_out, D1, not_1_out, S0);
  and and_3 (and_3_out, D2, S1, not_2_out);
  and and_4 (and_4_out, D3, S1, S0);
  or or_1 (Y, and_1_out, and_2_out, and_3_out, and_4_out);
endmodule

/* Test case:
S1 S0 D0 D1 D2 D3 Y
0  0  0  X  X  X  0
0  0  1  X  X  X  1
0  1  X  0  X  X  0
0  1  X  1  X  X  1
1  0  X  X  0  X  0
1  0  X  X  1  X  1
1  1  X  X  X  0  0
1  1  X  X  X  1  1
*/
