// Digital circuit 1.dig as structural Verilog
module _1 (
  input  S1,
  input  S0,
  input  D0,
  input  D1,
  input  D2,
  input  D3,
  input  D4,
  input  D5,
  input  D6,
  input  D7,
  input  D8,
  input  D9,
  input  D10,
  input  D11,
  input  D12,
  input  D13,
  input  D14,
  input  D15,
  output Y0,
  output Y1,
  output Y2,
  output Y3
);

  _1 _1_1 (.S1(S1), .S0(S0), .D3(D15), .D2(D14), .D1(D13), .D0(D12), .Y(Y3));
  _1 _1_2 (.S1(S1), .S0(S0), .D3(D11), .D2(D10), .D1(D9), .D0(D8), .Y(Y2));
  _1 _1_3 (.S1(S1), .S0(S0), .D3(D7), .D2(D6), .D1(D5), .D0(D4), .Y(Y1));
  _1 _1_4 (.S1(S1), .S0(S0), .D3(D3), .D2(D2), .D1(D1), .D0(D0), .Y(Y0));
endmodule

/* Test case:
S1 S0 D15 D14 D13 D12 D11 D10 D9 D8 D7 D6 D5 D4 D3 D2 D1 D0 Y3 Y2 Y1 Y0
0  0  1   1   0   0   1   0   1  0  1  1  1  0  1  0  0  1  0  0  0  1
0  1  1   1   0   0   1   0   1  0  1  1  1  0  1  0  0  1  0  1  1  0
1  0  1   1   0   0   1   0   1  0  1  1  1  0  1  0  0  1  1  0  1  0
1  1  1   1   0   0   1   0   1  0  1  1  1  0  1  0  0  1  1  1  1  1
0  0  0   0   1   1   0   1   0  1  0  0  0  1  0  1  1  0  1  1  1  0
0  1  0   0   1   1   0   1   0  1  0  0  0  1  0  1  1  0  1  0  0  1
1  0  0   0   1   1   0   1   0  1  0  0  0  1  0  1  1  0  0  1  0  1
1  1  0   0   1   1   0   1   0  1  0  0  0  1  0  1  1  0  0  0  0  0
*/
