// Digital circuit ALU.dig as structural Verilog
module ALU (
  input  A0,
  input  A1,
  input  A2,
  input  B0,
  input  B1,
  input  B2,
  input  C0,
  input  C1,
  output R0,
  output R1,
  output R2,
  output OVF
);

  wire [3:0] canvisignea_c2_1_r0, restadorc2_a___b_1_r0, sumadorc2_a_b_1_r0, transformarac2toasm_1_r0;

  CanviSigneA_C2 canvisignea_c2_1 (
    .A0(A0), .A1(A1), .A2(A2), .R0(canvisignea_c2_1_r0[0]), .R1(canvisignea_c2_1_r0[1]),
    .R2(canvisignea_c2_1_r0[2]), .C(canvisignea_c2_1_r0[3]));
  SumadorC2_A_B sumadorc2_a_b_1 (
    .A0(A0), .A1(A1), .A2(A2), .B0(B0), .B1(B1), .B2(B2), .R0(sumadorc2_a_b_1_r0[0]),
    .R1(sumadorc2_a_b_1_r0[1]), .R2(sumadorc2_a_b_1_r0[2]), .OVF(sumadorc2_a_b_1_r0[3]));
  RestadorC2_A___B restadorc2_a___b_1 (
    .A3(A0), .A4(A1), .A5(A2), .B3(B0), .B4(B1), .B5(B2), .R0(restadorc2_a___b_1_r0[0]),
    .R1(restadorc2_a___b_1_r0[1]), .R2(restadorc2_a___b_1_r0[2]), .OVF(restadorc2_a___b_1_r0[3]));
  TransformarAC2toASM transformarac2toasm_1 (
    .A0(A0), .A1(A1), .A2(A2), .R0(transformarac2toasm_1_r0[0]), .R1(transformarac2toasm_1_r0[1]),
    .R2(transformarac2toasm_1_r0[2]), .R3(transformarac2toasm_1_r0[3]));
  _1 _1_1 (
    .C0(C0), .C1(C1), .D0(canvisignea_c2_1_r0[0]), .D1(canvisignea_c2_1_r0[1]), .D2(canvisignea_c2_1_r0[2]),
    .D3(canvisignea_c2_1_r0[3]), .D4(sumadorc2_a_b_1_r0[0]), .D5(sumadorc2_a_b_1_r0[1]),
    .D6(sumadorc2_a_b_1_r0[2]), .D7(sumadorc2_a_b_1_r0[3]), .D8(restadorc2_a___b_1_r0[0]),
    .D9(restadorc2_a___b_1_r0[1]), .D10(restadorc2_a___b_1_r0[2]), .D11(restadorc2_a___b_1_r0[3]),
    .D12(transformarac2toasm_1_r0[0]), .D13(transformarac2toasm_1_r0[1]), .D14(transformarac2toasm_1_r0[2]),
    .D15(transformarac2toasm_1_r0[3]), .R0(R0), .R1(R1), .R2(R2), .R3(OVF));
endmodule
