// Digital circuit CanviSigneA(C2).dig as structural Verilog
module CanviSigneA_C2 (
  input  A0,
  input  A1,
  input  A2,
  output R0,
  output R1,
  output R2,
  output C
);

  wire fa_1_cout, fa_2_cout, not_1_out, not_2_out, not_3_out;

  not not_1 (not_1_out, A0);
  not not_2 (not_2_out, A1);
  not not_3 (not_3_out, A2);
  FA fa_1 (.A(not_1_out), .B(1'b1), .Cin(1'b0), .Y(R0), .Cout(fa_1_cout));
  FA fa_2 (.A(not_2_out), .B(fa_1_cout), .Cin(1'b0), .Y(R1), .Cout(fa_2_cout));
  FA fa_3 (.A(not_3_out), .B(fa_2_cout), .Cin(1'b0), .Y(R2), .Cout(C));
endmodule

/* Test case:
A2 A1 A0 R2 R1 R0 C
0  0  0  0  0  0  1
0  0  1  1  1  1  0
0  1  0  1  1  0  0
0  1  1  1  0  1  0
1  0  0  1  0  0  0
1  0  1  0  1  1  0
1  1  0  0  1  0  0
1  1  1  0  0  1  0
*/
