// Digital circuit FA.dig as structural Verilog
module FA (
  input  A,
  input  B,
  input  Cin,
  output Y,
  output Cout
);

  wire ha_1_c, ha_1_y, ha_2_c;

  HA ha_1 (.A(A), .B(B), .C(ha_1_c), .Y(ha_1_y));
  HA ha_2 (.A(ha_1_y), .B(Cin), .C(ha_2_c), .Y(Y));
  or or_1 (Cout, ha_1_c, ha_2_c);
endmodule

/* Test case:
Cin B A Cout Y
0 0 0 0 0
0 0 1 0 1
0 1 0 0 1
0 1 1 1 0
1 0 0 0 1
1 0 1 1 0
1 1 0 1 0
1 1 1 1 1
*/
