// Digital circuit HA.dig as structural Verilog
module HA (
  input  A,
  input  B,
  output C,
  output Y
);

  xor xor_1 (Y, A, B);
  and and_1 (C, A, B);
endmodule

/* Test case:
A B C Y
0 0 0 0
0 1 0 1
1 0 0 1
1 1 1 0
*/
