// Digital circuit 2.dig as structural Verilog
module _2 (
  input  A0,
  input  A1,
  input  B0,
  input  B1,
  input  S,
  output Y0,
  output Y1
);

  wire not_1_out;

  not not_1 (not_1_out, S);
  _1 _1_1 (.A(A0), .B(B0), .S(not_1_out), .Y(Y0));
  _1 _1_2 (.A(A1), .B(B1), .S(S), .Y(Y1));
endmodule

/* Test case:
S B1 B0 A1 A0 Y1 Y0
0 0 0 0 0 0 0
0 0 0 0 1 0 0
0 0 0 1 0 1 0
0 0 0 1 1 1 0
0 0 1 0 0 0 1
0 0 1 0 1 0 1
0 0 1 1 0 1 1
0 0 1 1 1 1 1
0 1 0 0 0 0 0
0 1 0 0 1 0 0
0 1 0 1 0 1 0
0 1 0 1 1 1 0
0 1 1 0 0 0 1
0 1 1 0 1 0 1
0 1 1 1 0 1 1
0 1 1 1 1 1 1
1 0 0 0 0 0 0
1 0 0 0 1 0 1
1 0 0 1 0 0 0
1 0 0 1 1 0 1
1 0 1 0 0 0 0
1 0 1 0 1 0 1
1 0 1 1 0 0 0
1 0 1 1 1 0 1
1 1 0 0 0 1 0
1 1 0 0 1 1 1
1 1 0 1 0 1 0
1 1 0 1 1 1 1
1 1 1 0 0 1 0
1 1 1 0 1 1 1
1 1 1 1 0 1 0
1 1 1 1 1 1 1
*/
