// Digital circuit RestadorC2(A+(-B)).dig as structural Verilog
module RestadorC2_A___B (
  input  A3,
  input  A4,
  input  A5,
  input  B3,
  input  B4,
  input  B5,
  output R0,
  output R1,
  output R2,
  output OVF
);

  wire fa_1_cout, fa_2_cout, fa_3_cout, not_1_out, not_2_out, not_3_out;

  not not_1 (not_1_out, B3);
  not not_2 (not_2_out, B4);
  not not_3 (not_3_out, B5);
  FA fa_1 (.A(A3), .B(not_1_out), .Cin(1'b1), .Y(R0), .Cout(fa_1_cout));
  FA fa_2 (.A(A4), .B(not_2_out), .Cin(fa_1_cout), .Y(R1), .Cout(fa_2_cout));
  FA fa_3 (.A(A5), .B(not_3_out), .Cin(fa_2_cout), .Y(R2), .Cout(fa_3_cout));
  xor xor_1 (OVF, fa_3_cout, fa_2_cout);
endmodule

/* Test case:
A5 A4 A3 B5 B4 B3 R2 R1 R0 OVF
0 0 0 0 0 0 0 0 0 0
0 0 0 0 0 1 1 1 1 0
0 0 0 0 1 0 1 1 0 0
0 0 0 0 1 1 1 0 1 0
0 0 0 1 0 0 1 0 0 1
0 0 0 1 0 1 0 1 1 0
0 0 0 1 1 0 0 1 0 0
0 0 0 1 1 1 0 0 1 0
0 0 1 0 0 0 0 0 1 0
0 0 1 0 0 1 0 0 0 0
0 0 1 0 1 0 1 1 1 0
0 0 1 0 1 1 1 1 0 0
0 0 1 1 0 0 1 0 1 1
0 0 1 1 0 1 1 0 0 1
0 0 1 1 1 0 0 1 1 0
0 0 1 1 1 1 0 1 0 0
0 1 0 0 0 0 0 1 0 0
0 1 0 0 0 1 0 0 1 0
0 1 0 0 1 0 0 0 0 0
0 1 0 0 1 1 1 1 1 0
0 1 0 1 0 0 1 1 0 1
0 1 0 1 0 1 1 0 1 1
0 1 0 1 1 0 1 0 0 1
0 1 0 1 1 1 0 1 1 0
0 1 1 0 0 0 0 1 1 0
0 1 1 0 0 1 0 1 0 0
0 1 1 0 1 0 0 0 1 0
0 1 1 0 1 1 0 0 0 0
0 1 1 1 0 0 1 1 1 1
0 1 1 1 0 1 1 1 0 1
0 1 1 1 1 0 1 0 1 1
0 1 1 1 1 1 1 0 0 1
1 0 0 0 0 0 1 0 0 0
1 0 0 0 0 1 0 1 1 1
1 0 0 0 1 0 0 1 0 1
1 0 0 0 1 1 0 0 1 1
1 0 0 1 0 0 0 0 0 0
1 0 0 1 0 1 1 1 1 0
1 0 0 1 1 0 1 1 0 0
1 0 0 1 1 1 1 0 1 0
1 0 1 0 0 0 1 0 1 0
1 0 1 0 0 1 1 0 0 0
1 0 1 0 1 0 0 1 1 1
1 0 1 0 1 1 0 1 0 1
1 0 1 1 0 0 0 0 1 0
1 0 1 1 0 1 0 0 0 0
1 0 1 1 1 0 1 1 1 0
1 0 1 1 1 1 1 1 0 0
1 1 0 0 0 0 1 1 0 0
1 1 0 0 0 1 1 0 1 0
1 1 0 0 1 0 1 0 0 0
1 1 0 0 1 1 0 1 1 1
1 1 0 1 0 0 0 1 0 0
1 1 0 1 0 1 0 0 1 0
1 1 0 1 1 0 0 0 0 0
1 1 0 1 1 1 1 1 1 0
1 1 1 0 0 0 1 1 1 0
1 1 1 0 0 1 1 1 0 0
1 1 1 0 1 0 1 0 1 0
1 1 1 0 1 1 1 0 0 0
1 1 1 1 0 0 0 1 1 0
1 1 1 1 0 1 0 1 0 0
1 1 1 1 1 0 0 0 1 0
1 1 1 1 1 1 0 0 0 0
*/
