// Digital circuit SumadorC2(A+B).dig as structural Verilog
module SumadorC2_A_B (
  input  A0,
  input  A1,
  input  A2,
  input  B0,
  input  B1,
  input  B2,
  output R0,
  output R1,
  output R2,
  output OVF
);

  wire fa_1_cout, fa_2_cout, fa_3_cout;

  FA fa_1 (.A(A0), .B(B0), .Cin(1'b0), .Y(R0), .Cout(fa_1_cout));
  FA fa_2 (.A(A1), .B(B1), .Cin(fa_1_cout), .Y(R1), .Cout(fa_2_cout));
  FA fa_3 (.A(A2), .B(B2), .Cin(fa_2_cout), .Y(R2), .Cout(fa_3_cout));
  xor xor_1 (OVF, fa_3_cout, fa_2_cout);
endmodule

/* Test case:
A2 A1 A0 B2 B1 B0 R2 R1 R0 OVF
0 0 0 0 0 0 0 0 0 0
0 0 0 0 0 1 0 0 1 0
0 0 0 0 1 0 0 1 0 0
0 0 0 0 1 1 0 1 1 0
0 0 0 1 0 0 1 0 0 0
0 0 0 1 0 1 1 0 1 0
0 0 0 1 1 0 1 1 0 0
0 0 0 1 1 1 1 1 1 0
0 0 1 0 0 0 0 0 1 0
0 0 1 0 0 1 0 1 0 0
0 0 1 0 1 0 0 1 1 0
0 0 1 0 1 1 1 0 0 1
0 0 1 1 0 0 1 0 1 0
0 0 1 1 0 1 1 1 0 0
0 0 1 1 1 0 1 1 1 0
0 0 1 1 1 1 0 0 0 0
0 1 0 0 0 0 0 1 0 0
0 1 0 0 0 1 0 1 1 0
0 1 0 0 1 0 1 0 0 1
0 1 0 0 1 1 1 0 1 1
0 1 0 1 0 0 1 1 0 0
0 1 0 1 0 1 1 1 1 0
0 1 0 1 1 0 0 0 0 0
0 1 0 1 1 1 0 0 1 0
0 1 1 0 0 0 0 1 1 0
0 1 1 0 0 1 1 0 0 1
0 1 1 0 1 0 1 0 1 1
0 1 1 0 1 1 1 1 0 1
0 1 1 1 0 0 1 1 1 0
0 1 1 1 0 1 0 0 0 0
0 1 1 1 1 0 0 0 1 0
0 1 1 1 1 1 0 1 0 0
1 0 0 0 0 0 1 0 0 0
1 0 0 0 0 1 1 0 1 0
1 0 0 0 1 0 1 1 0 0
1 0 0 0 1 1 1 1 1 0
1 0 0 1 0 0 0 0 0 1
1 0 0 1 0 1 0 0 1 1
1 0 0 1 1 0 0 1 0 1
1 0 0 1 1 1 0 1 1 1
1 0 1 0 0 0 1 0 1 0
1 0 1 0 0 1 1 1 0 0
1 0 1 0 1 0 1 1 1 0
1 0 1 0 1 1 0 0 0 0
1 0 1 1 0 0 0 0 1 1
1 0 1 1 0 1 0 1 0 1
1 0 1 1 1 0 0 1 1 1
1 0 1 1 1 1 1 0 0 0
1 1 0 0 0 0 1 1 0 0
1 1 0 0 0 1 1 1 1 0
1 1 0 0 1 0 0 0 0 0
1 1 0 0 1 1 0 0 1 0
1 1 0 1 0 0 0 1 0 1
1 1 0 1 0 1 0 1 1 1
1 1 0 1 1 0 1 0 0 0
1 1 0 1 1 1 1 0 1 0
1 1 1 0 0 0 1 1 1 0
1 1 1 0 0 1 0 0 0 0
1 1 1 0 1 0 0 0 1 0
1 1 1 0 1 1 0 1 0 0
1 1 1 1 0 0 0 1 1 1
1 1 1 1 0 1 1 0 0 0
1 1 1 1 1 0 1 0 1 0
1 1 1 1 1 1 1 1 0 0
*/
