// Digital circuit TransformarAC2toASM.dig as structural Verilog
module TransformarAC2toASM (
  input  A0,
  input  A1,
  input  A2,
  output R0,
  output R1,
  output R2,
  output R3
);

  wire and_2_out, and_3_out, not_1_out, not_2_out, not_3_out, xor_1_out;

  not not_1 (not_1_out, A2);
  not not_2 (not_2_out, A1);
  not not_3 (not_3_out, A0);
  xor xor_1 (xor_1_out, A0, A1);
  and and_1 (R1, not_3_out, not_2_out, A2);
  and and_2 (and_2_out, xor_1_out, A2);
  and and_3 (and_3_out, not_1_out, A1);
  or or_1 (R2, and_2_out, and_3_out);

  assign R0 = A0;
  assign R3 = A2;
endmodule

/* Test case:
A2 A1 A0 R3 R2 R1 R0
0 0 0 0 0 0 0
0 0 1 0 0 0 1
0 1 0 0 1 0 0
0 1 1 0 1 0 1
1 0 0 1 0 1 0
1 0 1 1 1 0 1
1 1 0 1 1 0 0
1 1 1 1 0 0 1
*/
