// Digital circuit showDisplay.dig as structural Verilog
module showDisplay (
  input  X0,
  input  X1,
  input  X2,
  output A,
  output B,
  output C,
  output D,
  output E,
  output F,
  output G,
  output H
);

  wire and_1_out, and_2_out, and_3_out, and_4_out, and_5_out, and_6_out, and_7_out, and_8_out, and_9_out,
       and_10_out, and_11_out, and_12_out, and_13_out, and_14_out, and_15_out, and_16_out, not_1_out,
       not_2_out, not_3_out;

  not not_1 (not_1_out, X2);
  not not_2 (not_2_out, X1);
  not not_3 (not_3_out, X0);
  and and_1 (and_1_out, not_1_out, not_3_out);
  and and_2 (and_2_out, X2, X0);
  and and_3 (and_3_out, not_2_out, not_3_out);
  and and_4 (and_4_out, X1, X0);
  and and_5 (and_5_out, not_1_out, not_3_out);
  and and_6 (and_6_out, not_1_out, X1);
  and and_7 (and_7_out, X2, not_2_out, X0);
  and and_8 (and_8_out, X1, not_3_out);
  and and_9 (and_9_out, not_1_out, not_3_out);
  and and_10 (and_10_out, X1, not_3_out);
  and and_11 (and_11_out, not_2_out, not_3_out);
  and and_12 (and_12_out, X2, not_2_out);
  and and_13 (and_13_out, X2, not_3_out);
  and and_14 (and_14_out, not_1_out, X1);
  and and_15 (and_15_out, X2, not_2_out);
  and and_16 (and_16_out, X1, not_3_out);
  or or_1 (A, and_1_out, X1, and_2_out);
  or or_2 (B, and_3_out, not_1_out, and_4_out);
  or or_3 (C, X2, not_2_out, X0);
  or or_4 (D, and_5_out, and_6_out, and_7_out, and_8_out);
  or or_5 (E, and_9_out, and_10_out);
  or or_6 (F, and_11_out, and_12_out, and_13_out);
  or or_7 (G, and_14_out, and_15_out, and_16_out);

  assign H = 1'b0;
endmodule

/* Test case:
X2	X1	X0	A	B	C	D	E	F	G	H
0	0	0	1	1	1	1	1	1	0	0
0	0	1	0	1	1	0	0	0	0	0
0	1	0	1	1	0	1	1	0	1	0
0	1	1	1	1	1	1	0	0	1	0
1	0	0	0	1	1	0	0	1	1	0
1	0	1	1	0	1	1	0	1	1	0
1	1	0	1	0	1	1	1	1	1	0
1	1	1	1	1	1	0	0	0	0	0
*/
