// Digital circuit solucio.dig as structural Verilog
module solucio (
  input  A0,
  input  A1,
  input  A2,
  input  B0,
  input  B1,
  input  B2,
  input  C0,
  input  C1,
  output R0,
  output R1,
  output R2
);

  wire alu_1_p12, and_1_out, muxc2sm_1_a, muxc2sm_1_b, muxc2sm_1_c, muxc2sm_1_d, muxc2sm_1_e, muxc2sm_1_f,
       muxc2sm_1_g, muxc2sm_1_h, showdisplay_1_a, showdisplay_1_b, showdisplay_1_c, showdisplay_1_d,
       showdisplay_1_e, showdisplay_1_f, showdisplay_1_g, showdisplay_1_h, showdisplay_2_a, showdisplay_2_b,
       showdisplay_2_c, showdisplay_2_d, showdisplay_2_e, showdisplay_2_f, showdisplay_2_g, showdisplay_2_h;

  and and_1 (and_1_out, C0, C1);
  Seven_Seg seven_seg_1 (.a(1'b0), .b(1'b0), .c(1'b0), .d(1'b0), .e(1'b0), .f(1'b0), .g(B2), .dp(1'b0));
  showDisplay showdisplay_1 (
    .X0(B0), .X1(B1), .X2(B2), .A(showdisplay_1_a), .B(showdisplay_1_b), .C(showdisplay_1_c),
    .D(showdisplay_1_d), .E(showdisplay_1_e), .F(showdisplay_1_f), .G(showdisplay_1_g), .H(showdisplay_1_h));
  Seven_Seg seven_seg_2 (.a(1'b0), .b(1'b0), .c(1'b0), .d(1'b0), .e(1'b0), .f(1'b0), .g(A2), .dp(1'b0));
  showDisplay showdisplay_2 (
    .X0(A0), .X1(A1), .X2(A2), .A(showdisplay_2_a), .B(showdisplay_2_b), .C(showdisplay_2_c),
    .D(showdisplay_2_d), .E(showdisplay_2_e), .F(showdisplay_2_f), .G(showdisplay_2_g), .H(showdisplay_2_h));
  // ALU alu_1: pin names not known; wires that end beside it: A0, A1, A2, B0, B1, B2, C0, C1, R0, R1, R2, alu_1_p12
  Seven_Seg seven_seg_3 (
    .a(showdisplay_1_a), .b(showdisplay_1_b), .c(showdisplay_1_c), .d(showdisplay_1_d), .e(showdisplay_1_e),
    .f(showdisplay_1_f), .g(showdisplay_1_g), .dp(showdisplay_1_h));
  Seven_Seg seven_seg_4 (
    .a(showdisplay_2_a), .b(showdisplay_2_b), .c(showdisplay_2_c), .d(showdisplay_2_d), .e(showdisplay_2_e),
    .f(showdisplay_2_f), .g(showdisplay_2_g), .dp(showdisplay_2_h));
  LED OVF (.in(alu_1_p12));
  Seven_Seg seven_seg_5 (.a(1'b0), .b(1'b0), .c(1'b0), .d(1'b0), .e(1'b0), .f(1'b0), .g(alu_1_p12), .dp(1'b0));
  MUXC2SM muxc2sm_1 (
    .R0(R0), .R1(R1), .R2(R2), .R3(alu_1_p12), .S(and_1_out), .A(muxc2sm_1_a), .B(muxc2sm_1_b),
    .C(muxc2sm_1_c), .D(muxc2sm_1_d), .E(muxc2sm_1_e), .F(muxc2sm_1_f), .G(muxc2sm_1_g), .H(muxc2sm_1_h));
  Seven_Seg seven_seg_6 (
    .a(muxc2sm_1_a), .b(muxc2sm_1_b), .c(muxc2sm_1_c), .d(muxc2sm_1_d), .e(muxc2sm_1_e), .f(muxc2sm_1_f),
    .g(muxc2sm_1_g), .dp(muxc2sm_1_h));
endmodule
