// Digital circuit 3Bit-Comparator.dig as structural Verilog
module _3Bit_Comparator (
  input  A0,
  input  A1,
  input  A2,
  input  B0,
  input  B1,
  input  B2,
  output Y
);

  wire xnor_1_out, xnor_2_out, xnor_3_out;

  xnor xnor_1 (xnor_1_out, A0, B0);
  xnor xnor_2 (xnor_2_out, A1, B1);
  xnor xnor_3 (xnor_3_out, A2, B2);
  and and_1 (Y, xnor_1_out, xnor_2_out, xnor_3_out);
endmodule
