// Digital circuit 3BitSuperComparator.dig as structural Verilog
module _3BitSuperComparator (
  input  A0,
  input  A1,
  input  A2,
  input  B0,
  input  B1,
  input  B2,
  output A__eq__B,
  output A__gt__B,
  output A__lt__B
);

  wire _2bit_comparator_1_p3, _2bit_comparator_1_p4, _2bit_comparator_1_p5, _2bit_comparator_2_p3,
       _2bit_comparator_2_p4, _2bit_comparator_2_p5, _2bit_comparator_3_p3, _2bit_comparator_3_p4,
       _2bit_comparator_3_p5, and_1_out, and_2_out, and_3_out, and_4_out, or_1_out, or_2_out;

  // _2Bit_Comparator _2bit_comparator_1: pin names not known; wires that end beside it: A2, B2, _2bit_comparator_1_p3, _2bit_comparator_1_p4, _2bit_comparator_1_p5
  // _2Bit_Comparator _2bit_comparator_2: pin names not known; wires that end beside it: A1, B1, _2bit_comparator_2_p3, _2bit_comparator_2_p4, _2bit_comparator_2_p5
  // _2Bit_Comparator _2bit_comparator_3: pin names not known; wires that end beside it: A0, B0, _2bit_comparator_3_p3, _2bit_comparator_3_p4, _2bit_comparator_3_p5
  and and_1 (and_1_out, _2bit_comparator_1_p4, _2bit_comparator_2_p3);
  and and_2 (and_2_out, _2bit_comparator_1_p4, _2bit_comparator_2_p4, _2bit_comparator_3_p3);
  and and_3 (and_3_out, _2bit_comparator_1_p5, _2bit_comparator_2_p4, _2bit_comparator_3_p4);
  and and_4 (and_4_out, _2bit_comparator_2_p5, _2bit_comparator_3_p4);
  or or_1 (or_1_out, and_1_out, and_2_out);
  or or_2 (or_2_out, and_3_out, and_4_out);
  or or_3 (A__lt__B, _2bit_comparator_1_p3, or_1_out);
  and and_5 (A__eq__B, _2bit_comparator_1_p4, _2bit_comparator_2_p4, _2bit_comparator_3_p4);
  or or_4 (A__gt__B, or_2_out, _2bit_comparator_3_p5);
endmodule
