// Digital circuit 4Bit-Substracter.dig as structural Verilog
module _4Bit_Substracter (
  input  A0,
  input  A1,
  input  A2,
  input  B0,
  input  B1,
  input  B2,
  output S0,
  output S1,
  output S2,
  output Cout
);

  wire full_substracter_1_cout, full_substracter_2_cout;

  Full_Substracter full_substracter_1 (.A(A0), .B(B0), .Cin(1'b0), .S(S0), .Cout(full_substracter_1_cout));
  Full_Substracter full_substracter_2 (
    .A(A1), .B(B1), .Cin(full_substracter_1_cout), .S(S1), .Cout(full_substracter_2_cout));
  Full_Substracter full_substracter_3 (.A(A2), .B(B2), .Cin(full_substracter_2_cout), .S(S2), .Cout(Cout));
endmodule
