// Digital circuit 5Bit-AdderSM - Copy.dig as structural Verilog
module _5Bit_AdderSM___Copy (
  input  A0,
  input  A1,
  input  A2,
  input  A3,
  input  B0,
  input  B1,
  input  B2,
  input  B3,
  output S0,
  output S1,
  output S2,
  output S3,
  output S4
);

  wire _3bitsupercomparator_1_a__eq__b, _3bitsupercomparator_1_a__gt__b, _3bitsupercomparator_1_a__lt__b,
       _4bit_adder_1_p7, _4bit_adder_1_p8, _4bit_adder_1_p9, _4bit_adder_1_p10, _4bit_substracter_1_cout,
       _4bit_substracter_1_s0, _4bit_substracter_1_s1, _4bit_substracter_1_s2, and_3_out, xor_1_out;
  wire [1:0] and_1_out;
  wire [3:0] multiplexer_1_out, multiplexer_2_out;

  xor xor_1 (xor_1_out, A3, B3);
  // _4Bit_Adder _4bit_adder_1: pin names not known; wires that end beside it: A0, A1, A2, B0, B1, B2, _4bit_adder_1_p7, _4bit_adder_1_p8, _4bit_adder_1_p9, _4bit_adder_1_p10
  _4Bit_Substracter _4bit_substracter_1 (
    .A0(A0), .A1(A1), .A2(A2), .B0(B0), .B1(B1), .B2(B2), .S0(_4bit_substracter_1_s0),
    .S1(_4bit_substracter_1_s1), .S2(_4bit_substracter_1_s2), .Cout(_4bit_substracter_1_cout));
  _3BitSuperComparator _3bitsupercomparator_1 (
    .A0(A0), .A1(A1), .A2(A2), .B0(B0), .B1(B1), .B2(B2), .A__eq__B(_3bitsupercomparator_1_a__eq__b),
    .A__gt__B(_3bitsupercomparator_1_a__gt__b), .A__lt__B(_3bitsupercomparator_1_a__lt__b));
  and and_1 (and_1_out[0], _3bitsupercomparator_1_a__lt__b, xor_1_out);
  and and_2 (and_1_out[1], _3bitsupercomparator_1_a__gt__b, xor_1_out);
  Multiplexer #(.Selector_Bits(2)) multiplexer_1 (
    .sel(and_1_out), .in_0(_4bit_adder_1_p7), .in_1(_4bit_adder_1_p8), .in_2(_4bit_adder_1_p9),
    .in_3(_4bit_adder_1_p10), .out(multiplexer_1_out[0]));
  Multiplexer #(.Selector_Bits(2)) multiplexer_2 (
    .sel(and_1_out), .in_0(_4bit_substracter_1_s0), .in_1(_4bit_substracter_1_s1),
    .in_2(_4bit_substracter_1_s2), .in_3(_4bit_substracter_1_cout), .out(multiplexer_2_out[0]));
  and and_3 (and_3_out, _3bitsupercomparator_1_a__eq__b, xor_1_out);
  or or_1 (S4, and_1_out[1], and_1_out[0]);
  or or_2 (S0, multiplexer_1_out[0], and_3_out, multiplexer_2_out[0]);
  or or_3 (S1, multiplexer_1_out[1], and_3_out, multiplexer_2_out[1]);
  or or_4 (S2, multiplexer_1_out[2], and_3_out, multiplexer_2_out[2]);
  or or_5 (S3, multiplexer_1_out[3], and_3_out, multiplexer_2_out[3]);
  // Pins of 1 and 4 bits meet at multiplexer_2_out
  // Pins of 1 and 4 bits meet at multiplexer_1_out
endmodule
