// Digital circuit 5Bit-AdderSM.dig as structural Verilog
module _5Bit_AdderSM (
  input  A0,
  input  A1,
  input  A2,
  input  A3,
  input  B0,
  input  B1,
  input  B2,
  input  B3,
  output S0,
  output S1,
  output S2,
  output S3,
  output S4
);

  wire _4bit_adder_1_p7, _4bit_adder_1_p8, _4bit_adder_1_p9, _4bit_adder_1_p10, _4bit_substracter_1_cout,
       _4bit_substracter_1_s0, _4bit_substracter_1_s1, _4bit_substracter_1_s2, maxminselector_1_a__eq__b,
       maxminselector_1_a__gt__b, maxminselector_1_a__lt__b, maxminselector_1_x0, maxminselector_1_x1,
       maxminselector_1_x2, maxminselector_1_y0, maxminselector_1_y1, maxminselector_1_y2, xor_1_out;

  // _4Bit_Adder _4bit_adder_1: pin names not known; wires that end beside it: A0, A1, A2, B0, B1, B2, _4bit_adder_1_p7, _4bit_adder_1_p8, _4bit_adder_1_p9, _4bit_adder_1_p10
  MaxMinSelector maxminselector_1 (
    .A0(A0), .A1(A1), .A2(A2), .B0(B0), .B1(B1), .B2(B2), .X0(maxminselector_1_x0), .X1(maxminselector_1_x1),
    .X2(maxminselector_1_x2), .Y0(maxminselector_1_y0), .Y1(maxminselector_1_y1), .Y2(maxminselector_1_y2),
    .A__eq__B(maxminselector_1_a__eq__b), .A__gt__B(maxminselector_1_a__gt__b),
    .A__lt__B(maxminselector_1_a__lt__b));
  xor xor_1 (xor_1_out, A3, B3);
  _4Bit_Substracter _4bit_substracter_1 (
    .A0(maxminselector_1_x0), .A1(maxminselector_1_x1), .A2(maxminselector_1_x2), .B0(maxminselector_1_y0),
    .B1(maxminselector_1_y1), .B2(maxminselector_1_y2), .S0(_4bit_substracter_1_s0),
    .S1(_4bit_substracter_1_s1), .S2(_4bit_substracter_1_s2), .Cout(_4bit_substracter_1_cout));
  GestionDelSigno gestiondelsigno_1 (
    .E(maxminselector_1_a__eq__b), .G(maxminselector_1_a__gt__b), .L(maxminselector_1_a__lt__b), .A(A3),
    .B(B3), .S(S4));
  MUX mux_1 (.A0(_4bit_adder_1_p7), .A1(_4bit_substracter_1_s0), .S(xor_1_out), .Y(S0));
  MUX mux_2 (.A0(_4bit_adder_1_p8), .A1(_4bit_substracter_1_s1), .S(xor_1_out), .Y(S1));
  MUX mux_3 (.A0(_4bit_adder_1_p9), .A1(_4bit_substracter_1_s2), .S(xor_1_out), .Y(S2));
  MUX mux_4 (.A0(_4bit_adder_1_p10), .A1(_4bit_substracter_1_cout), .S(xor_1_out), .Y(S3));
endmodule
