// Digital circuit 5Bit-Comparator.dig as structural Verilog
module _5Bit_Comparator (
  input  A0,
  input  B0,
  input  C0,
  input  D0,
  input  E0,
  input  A1,
  input  B1,
  input  C1,
  input  D1,
  input  E1,
  output Y
);

  wire xnor_1_out, xnor_2_out, xnor_3_out, xnor_4_out, xnor_5_out;

  xnor xnor_1 (xnor_1_out, A0, A1);
  xnor xnor_2 (xnor_2_out, B0, B1);
  xnor xnor_3 (xnor_3_out, C0, C1);
  xnor xnor_4 (xnor_4_out, D0, D1);
  xnor xnor_5 (xnor_5_out, E0, E1);
  and and_1 (Y, xnor_1_out, xnor_2_out, xnor_3_out, xnor_4_out, xnor_5_out);
endmodule
