// Digital circuit 7Bit-Decoder.dig as structural Verilog
module _7Bit_Decoder (
  input  A0,
  input  A1,
  input  E0,
  input  E1,
  output Y0,
  output Y1,
  output Y2,
  output Y3,
  output Y4,
  output Y5,
  output Y6,
  output Y7
);

  wire decoder_1_p4, decoder_1_p5, decoder_1_p6, decoder_1_p7;

  // Decoder decoder_1: pin names not known; wires that end beside it: A0, A1, E0, decoder_1_p4, decoder_1_p5, decoder_1_p6, decoder_1_p7
  // Decoder decoder_2: pin names not known; wires that end beside it: decoder_1_p4, decoder_1_p5, E1, Y0, Y1, Y2, Y3
  // Decoder decoder_3: pin names not known; wires that end beside it: decoder_1_p6, decoder_1_p7, E1, Y4, Y5, Y6, Y7
endmodule
