// Digital circuit 7BitMUX.dig as structural Verilog
module _7BitMUX (
  input  A0,
  input  A1,
  input  A2,
  input  A3,
  input  S0,
  input  S1,
  output Y
);

  wire mux_1_y, mux_2_y;

  MUX mux_1 (.A0(A0), .A1(A1), .S(S0), .Y(mux_1_y));
  MUX mux_2 (.A0(A2), .A1(A3), .S(S0), .Y(mux_2_y));
  MUX mux_3 (.A0(mux_1_y), .A1(mux_2_y), .S(S1), .Y(Y));
endmodule
