// Digital circuit ComparatorX.dig as structural Verilog
module ComparatorX (
  input  A,
  input  B,
  output A__lt__B,
  output A__eq__B,
  output A__gt__B
);

  wire not_1_out, not_2_out;

  not not_1 (not_1_out, A);
  not not_2 (not_2_out, B);
  and and_1 (A__lt__B, not_1_out, B);
  and and_2 (A__gt__B, A, not_2_out);
  nor nor_1 (A__eq__B, A__lt__B, A__gt__B);
endmodule
