// Digital circuit Decoder.dig as structural Verilog
module Decoder (
  input  A0,
  input  A1,
  input  E,
  output Y0,
  output Y1,
  output Y2,
  output Y3
);

  wire and_1_out, and_2_out, and_3_out, and_4_out, not_1_out, not_2_out;

  not not_1 (not_1_out, A0);
  not not_2 (not_2_out, A1);
  and and_1 (and_1_out, not_1_out, not_2_out);
  and and_2 (and_2_out, A0, not_2_out);
  and and_3 (and_3_out, not_1_out, A1);
  and and_4 (and_4_out, A0, not_2_out);
  and and_5 (Y0, and_1_out, E);
  and and_6 (Y1, and_2_out, E);
  and and_7 (Y2, and_3_out, E);
  and and_8 (Y3, and_4_out, E);
endmodule
