// Digital circuit Full-Adder.dig as structural Verilog
module Full_Adder (
  input  A,
  input  B,
  input  Cin,
  output S,
  output Cout
);

  wire half_adder_1_c, half_adder_2_c, half_adder_2_s;

  Half_Adder half_adder_1 (.A(A), .B(B), .S(S), .C(half_adder_1_c));
  Half_Adder half_adder_2 (.A(Cin), .B(half_adder_1_c), .S(half_adder_2_s), .C(half_adder_2_c));
  or or_1 (Cout, half_adder_2_s, half_adder_2_c);
endmodule
