// Digital circuit Full-Substracter.dig as structural Verilog
module Full_Substracter (
  input  A,
  input  B,
  input  Cin,
  output S,
  output Cout
);

  wire half_substracter_1_r, half_substracter_2_r, half_substracter_2_s;

  Half_Substracter half_substracter_1 (.A(A), .B(B), .S(S), .R(half_substracter_1_r));
  Half_Substracter half_substracter_2 (
    .A(Cin), .B(half_substracter_1_r), .S(half_substracter_2_s), .R(half_substracter_2_r));
  or or_1 (Cout, half_substracter_2_s, half_substracter_2_r);
endmodule
