// Digital circuit GestionDelSigno.dig as structural Verilog
module GestionDelSigno (
  input  E,
  input  G,
  input  L,
  input  A,
  input  B,
  output S
);

  wire and_1_out, and_2_out, or_1_out;

  or or_1 (or_1_out, G, E);
  and and_1 (and_1_out, A, or_1_out);
  and and_2 (and_2_out, L, B);
  or or_2 (S, and_1_out, and_2_out);
endmodule
