// Digital circuit Half-Adder.dig as structural Verilog
module Half_Adder (
  input  A,
  input  B,
  output S,
  output C
);

  xor xor_1 (S, A, B);
  and and_1 (C, A, B);
endmodule

/* Test case:
A B S C
0 0 0 0
0 1 1 0
1 0 1 0
1 1 0 1
*/
