// Digital circuit MAIN.dig as structural Verilog
module MAIN (
  input  Signo___U3,
  input  U2,
  input  U1,
  input  U0,
  input  Signo___V3,
  input  V2,
  input  V1,
  input  V0,
  input  Signo___C4,
  input  C3,
  input  C2,
  input  C1,
  input  C0,
  input  Signo___D4,
  input  D3,
  input  D2,
  input  D1,
  input  D0,
  output YU,
  output YV,
  output YD,
  output YC
);

  wire _5bit_addersm_1_s0, _5bit_addersm_1_s1, _5bit_addersm_1_s2, _5bit_addersm_1_s3, _5bit_addersm_1_s4,
       and_1_out, showdisplay_1_a, showdisplay_1_b, showdisplay_1_c, showdisplay_1_d, showdisplay_1_e,
       showdisplay_1_f, showdisplay_1_g, showdisplay_2_a, showdisplay_2_b, showdisplay_2_c, showdisplay_2_d,
       showdisplay_2_e, showdisplay_2_f, showdisplay_2_g;
  wire [3:0] rom_1_d, rom_2_d;

  ROM #(.AddrBits(1), .Bits(4)) rom_1 (.A(1'b1), .sel(1'b1), .D(rom_1_d));
  ROM #(.AddrBits(1), .Bits(4)) rom_2 (.A(1'b1), .sel(1'b1), .D(rom_2_d));
  _4Bit_ComparatorSM _4bit_comparatorsm_1 (
    .A0(U0), .A1(U1), .A2(U2), .A3(Signo___U3), .B0(rom_1_d[0]), .B1(rom_1_d[1]), .B2(rom_1_d[2]),
    .B3(rom_1_d[3]), .Y(YU));
  _5Bit_AdderSM _5bit_addersm_1 (
    .A0(rom_1_d[0]), .A1(rom_1_d[1]), .A2(rom_1_d[2]), .A3(rom_1_d[3]), .B0(rom_2_d[0]), .B1(rom_2_d[1]),
    .B2(rom_2_d[2]), .B3(rom_2_d[3]), .S0(_5bit_addersm_1_s0), .S1(_5bit_addersm_1_s1),
    .S2(_5bit_addersm_1_s2), .S3(_5bit_addersm_1_s3), .S4(_5bit_addersm_1_s4));
  _4Bit_ComparatorSM _4bit_comparatorsm_2 (
    .A0(rom_2_d[0]), .A1(rom_2_d[1]), .A2(rom_2_d[2]), .A3(rom_2_d[3]), .B0(V0), .B1(V1), .B2(V2),
    .B3(Signo___V3), .Y(YV));
  _5Bit_ComparatorSM _5bit_comparatorsm_1 (
    .A0(C0), .A1(C1), .A2(C2), .A3(C3), .A4(Signo___C4), .B0(_5bit_addersm_1_s0), .B1(_5bit_addersm_1_s1),
    .B2(_5bit_addersm_1_s2), .B3(_5bit_addersm_1_s3), .B4(_5bit_addersm_1_s4), .Y(YC));
  _5Bit_ComparatorSM _5bit_comparatorsm_2 (
    .A0(_5bit_addersm_1_s0), .A1(_5bit_addersm_1_s1), .A2(_5bit_addersm_1_s2), .A3(_5bit_addersm_1_s3),
    .A4(_5bit_addersm_1_s4), .B0(D0), .B1(D1), .B2(D2), .B3(D3), .B4(Signo___D4), .Y(YD));
  showDisplay showdisplay_1 (
    .X(YC), .Y(YU), .A(showdisplay_1_a), .B(showdisplay_1_b), .C(showdisplay_1_c), .D(showdisplay_1_d),
    .E(showdisplay_1_e), .F(showdisplay_1_f), .G(showdisplay_1_g));
  and and_1 (and_1_out, YC, YU, YV, YD);
  showDisplay showdisplay_2 (
    .X(YD), .Y(YV), .A(showdisplay_2_a), .B(showdisplay_2_b), .C(showdisplay_2_c), .D(showdisplay_2_d),
    .E(showdisplay_2_e), .F(showdisplay_2_f), .G(showdisplay_2_g));
  Seven_Seg seven_seg_1 (
    .a(showdisplay_1_a), .b(showdisplay_1_b), .c(showdisplay_1_c), .d(showdisplay_1_d), .e(showdisplay_1_e),
    .f(showdisplay_1_f), .g(showdisplay_1_g), .dp(1'b0));
  Seven_Seg seven_seg_2 (
    .a(showdisplay_2_a), .b(showdisplay_2_b), .c(showdisplay_2_c), .d(showdisplay_2_d), .e(showdisplay_2_e),
    .f(showdisplay_2_f), .g(showdisplay_2_g), .dp(1'b0));
  LED Y (.in(and_1_out));

  // Notes on the sheet:
  //   contents of rom_1 (hex, n*v repeats v):
  //   0,e,8*0,1
  //   contents of rom_2 (hex, n*v repeats v):
  //   0,2,8*0,1
endmodule
