// Digital circuit MUX.dig as structural Verilog
module MUX (
  input  A0,
  input  A1,
  input  S,
  output Y
);

  wire and_1_out, and_2_out, not_1_out;

  not not_1 (not_1_out, S);
  and and_1 (and_1_out, A0, not_1_out);
  and and_2 (and_2_out, A1, S);
  or or_1 (Y, and_1_out, and_2_out);
endmodule
