// Digital circuit MaxMinSelector.dig as structural Verilog
module MaxMinSelector (
  input  A0,
  input  A1,
  input  A2,
  input  B0,
  input  B1,
  input  B2,
  output X0,
  output X1,
  output X2,
  output Y0,
  output Y1,
  output Y2,
  output A__eq__B,
  output A__gt__B,
  output A__lt__B
);

  _3BitSuperComparator _3bitsupercomparator_1 (
    .A0(A0), .A1(A1), .A2(A2), .B0(B0), .B1(B1), .B2(B2), .A__eq__B(A__eq__B), .A__gt__B(A__gt__B),
    .A__lt__B(A__lt__B));
  MUX mux_1 (.A0(A2), .A1(B2), .S(A__lt__B), .Y(X2));
  MUX mux_2 (.A0(A1), .A1(B1), .S(A__lt__B), .Y(X1));
  MUX mux_3 (.A0(A0), .A1(B0), .S(A__lt__B), .Y(X0));
  MUX mux_4 (.A0(B2), .A1(A2), .S(A__lt__B), .Y(Y2));
  MUX mux_5 (.A0(B1), .A1(A1), .S(A__lt__B), .Y(Y1));
  MUX mux_6 (.A0(B0), .A1(A0), .S(A__lt__B), .Y(Y0));
endmodule
