// Digital circuit Substracter.dig as structural Verilog
module Substracter (
  input  A,
  input  B,
  input  Cin,
  output S,
  output Cout
);

  wire half_substracter_1_r, half_substracter_1_s, half_substracter_2_s;

  Half_Substracter half_substracter_1 (.A(A), .B(B), .S(half_substracter_1_s), .R(half_substracter_1_r));
  Half_Substracter half_substracter_2 (.A(half_substracter_1_r), .B(Cin), .S(half_substracter_2_s), .R(Cout));
  or or_1 (S, half_substracter_1_s, half_substracter_2_s);
endmodule
