// Digital circuit CodificarEntrades.dig as structural Verilog
module CodificarEntrades (
  input  M,
  input  Pup,
  input  Pdw,
  input  Cup,
  input  Cdw,
  output X2,
  output X1,
  output X0
);

  wire and_1_out, and_2_out, and_3_out, not_1_out;

  not not_1 (not_1_out, M);
  and and_1 (and_1_out, M, Pdw);
  and and_2 (and_2_out, not_1_out, Pdw);
  and and_3 (and_3_out, M, Pup);
  or or_1 (X2, Pup, and_1_out);
  or or_2 (X1, and_2_out, Cup, and_3_out);
  or or_3 (X0, Pdw, Cdw);

  // Notes on the sheet:
  //   M: 0 ⇢ Manual
  //   1 ⇢ Automatic
endmodule
