// Digital circuit J1.dig as structural Verilog
module J1 (
  input  X2,
  input  X1,
  input  X0,
  input  Q2,
  input  Q1,
  input  Q0,
  output J1
);

  wire not_6_out;

  // Not not_1 has open pins: in=Q2, out=open
  // Not not_2 has open pins: in=Q1, out=open
  // Not not_3 has open pins: in=Q0, out=open
  // Not not_4 has open pins: in=X2, out=open
  // Not not_5 has open pins: in=X1, out=open
  not not_6 (not_6_out, X0);
  and and_1 (J1, Q0, X1, not_6_out);

  // Notes on the sheet:
  //   X2: 0 ⇢ Manual
  //   1 ⇢ Automatic
endmodule
