// Digital circuit K0.dig as structural Verilog
module K0 (
  input  X2,
  input  X1,
  input  X0,
  input  Q2,
  input  Q1,
  input  Q0,
  output K0
);

  wire and_1_out, nor_1_out;

  // Not not_1 has open pins: in=Q2, out=open
  // Not not_2 has open pins: in=Q1, out=open
  // Not not_3 has open pins: in=Q0, out=open
  // Not not_4 has open pins: in=X2, out=open
  // Not not_5 has open pins: in=X1, out=open
  // Not not_6 has open pins: in=X0, out=open
  nor nor_1 (nor_1_out, X0, X1);
  and and_1 (and_1_out, Q1, X1);
  or or_1 (K0, nor_1_out, and_1_out);

  // Notes on the sheet:
  //   X2: 0 ⇢ Manual
  //   1 ⇢ Automatic
endmodule
