// Digital circuit K1.dig as structural Verilog
module K1 (
  input  X2,
  input  X1,
  input  X0,
  input  Q2,
  input  Q1,
  input  Q0,
  output K1
);

  wire not_3_out, not_5_out;

  // Not not_1 has open pins: in=Q2, out=open
  // Not not_2 has open pins: in=Q1, out=open
  not not_3 (not_3_out, Q0);
  // Not not_4 has open pins: in=X2, out=open
  not not_5 (not_5_out, X1);
  // Not not_6 has open pins: in=X0, out=open
  and and_1 (K1, not_3_out, not_5_out, X0);

  // Notes on the sheet:
  //   X2: 0 ⇢ Manual
  //   1 ⇢ Automatic
endmodule
