// Digital circuit K2.dig as structural Verilog
module K2 (
  input  X2,
  input  X1,
  input  X0,
  input  Q2,
  input  Q1,
  input  Q0,
  output K2
);

  wire and_1_out, not_4_out, not_5_out, not_6_out;

  // Not not_1 has open pins: in=Q2, out=open
  // Not not_2 has open pins: in=Q1, out=open
  // Not not_3 has open pins: in=Q0, out=open
  not not_4 (not_4_out, X2);
  not not_5 (not_5_out, X1);
  not not_6 (not_6_out, X0);
  and and_1 (and_1_out, not_4_out, not_5_out);
  or or_1 (K2, not_6_out, and_1_out);

  // Notes on the sheet:
  //   X2: 0 ⇢ Manual
  //   1 ⇢ Automatic
endmodule
