// Digital circuit PL.dig as structural Verilog
module PL (
  input  X2,
  input  X1,
  input  X0,
  input  Q2,
  input  Q1,
  input  Q0,
  output PL
);

  wire and_1_out, and_2_out, not_4_out, not_6_out, or_1_out;

  // Not not_1 has open pins: in=X2, out=open
  // Not not_2 has open pins: in=X1, out=open
  // Not not_3 has open pins: in=X0, out=open
  not not_4 (not_4_out, Q2);
  // Not not_5 has open pins: in=Q1, out=open
  not not_6 (not_6_out, Q0);
  or or_1 (or_1_out, X2, X1);
  and and_1 (and_1_out, or_1_out, X0, not_4_out);
  and and_2 (and_2_out, Q2, X2, not_6_out);
  or or_2 (PL, and_1_out, and_2_out);

  // Notes on the sheet:
  //   X2: 0 ⇢ Manual
  //   1 ⇢ Automatic
endmodule
