// Digital circuit PinyoDisplay.dig as structural Verilog
module PinyoDisplay (
  input  X,
  input  Y,
  output A,
  output B,
  output C,
  output D,
  output E,
  output F,
  output G,
  output H
);

  wire and_1_out, not_1_out, not_2_out;

  not not_1 (not_1_out, X);
  not not_2 (not_2_out, Y);
  xor xor_1 (A, Y, X);
  and and_1 (and_1_out, not_1_out, not_2_out);
  and and_2 (E, not_1_out, Y);
  and and_3 (F, X, Y);
  or or_1 (G, X, Y);
  or or_2 (C, X, and_1_out);

  assign B = 1'b1;
  assign D = A;
  assign H = 1'b0;
endmodule
