// Digital circuit PlateDisplay.dig as structural Verilog
module PlateDisplay (
  input  P,
  output A,
  output B,
  output C,
  output D,
  output E,
  output F,
  output G,
  output H
);

  not not_1 (C, P);

  assign A = P;
  assign B = 1'b1;
  assign D = P;
  assign E = P;
  assign F = 1'b0;
  assign G = P;
  assign H = 1'b0;
endmodule
