// Digital circuit SequentialCircuit.dig as structural Verilog
module SequentialCircuit (
  input  CLK,
  input  X2,
  input  X1,
  input  X0,
  output Q2,
  output PL,
  output Q1,
  output Q0,
  output CL
);

  wire j0_1_j0, j1_1_j1, j2_1_j2, k0_1_k0, k1_1_k1, k2_1_k2;

  J2 j2_1 (.X2(X2), .X1(X1), .X0(X0), .Q2(Q2), .Q1(Q1), .Q0(Q0), .J2(j2_1_j2));
  K2 k2_1 (.X2(X2), .X1(X1), .X0(X0), .Q2(Q2), .Q1(Q1), .Q0(Q0), .K2(k2_1_k2));
  J1 j1_1 (.X2(X2), .X1(X1), .X0(X0), .Q2(Q2), .Q1(Q1), .Q0(Q0), .J1(j1_1_j1));
  K1 k1_1 (.X2(X2), .X1(X1), .X0(X0), .Q2(Q2), .Q1(Q1), .Q0(Q0), .K1(k1_1_k1));
  J0 j0_1 (.X2(X2), .X1(X1), .X0(X0), .Q2(Q2), .Q1(Q1), .Q0(Q0), .J0(j0_1_j0));
  K0 k0_1 (.X2(X2), .X1(X1), .X0(X0), .Q2(Q2), .Q1(Q1), .Q0(Q0), .K0(k0_1_k0));
  JK_FF FF2 (.J(j2_1_j2), .C(CLK), .K(k2_1_k2), .Q(Q2));  // open: nQ
  PL pl_1 (.X2(X2), .X1(X1), .X0(X0), .Q2(Q2), .Q1(Q1), .Q0(Q0), .PL(PL));
  JK_FF FF1 (.J(j1_1_j1), .C(CLK), .K(k1_1_k1), .Q(Q1));  // open: nQ
  JK_FF FF0 (.J(j0_1_j0), .C(CLK), .K(k0_1_k0), .Q(Q0));  // open: nQ
  CL cl_1 (.X2(X2), .X1(X1), .X0(X0), .Q2(Q2), .Q1(Q1), .Q0(Q0), .CL(CL));
endmodule
